// Digital circuit clima.dig as structural Verilog
module clima (
  input  [6:0] a,
  input  [6:0] b,
  output [3:0] saida
);

  test_int #(.applicationType("GHDL")) u_test_int (.a(a), .b(b), .t_out(saida));
endmodule

/* Code of test_int:
library ieee;
use ieee.std_logic_1164.all;
use ieee.numeric_std.all;

--------------------------------------------------

entity test_int is
port(	
    a: in std_logic_vector(6 downto 0);
    b: in std_logic_vector(6 downto 0);
   -- c: in integer;
	t_out: out std_logic_vector(3 downto 0)
);
end test_int;  

--------------------------------------------------

architecture behav_add of test_int is
    Signal vl1 : integer range  -10 to 50;
    Signal vl2 : integer range  -10 to 50;
    Signal vl_avg : integer range  -20 to 100;
begin
    process(a,b)
    begin
        vl1 <= to_integer(signed(a));
        vl2 <= to_integer(signed(b));

        vl_avg <= (vl1+vl2);

        if vl_avg < 0 then
            t_out <= "0001";
        elsif vl_avg < 15 then 
            t_out <= "0010";
        elsif vl_avg < 20 then
            t_out <= "0100";
	ELSE 
	        t_out <= "1000";
        end if;
            
    end process;

end behav_add;

--------------------------------------------------
*/
